# Fritzing sketch Pi_DMX_Board (saved by Fritzing 0.9.3b)
circuit board: 8.46667cm x 5.64444cm
breadboards: 1

parts:
  U1 = MAX485 [package=dil08]
  Atmega162 = ATmega162 [package=pdpi]
  Raspberry_Pi_1 = Raspberry Pi 3 [part_number=RPI-3-V1.2]
  R2 = Resistor [tolerance=±5% resistance=1.6k package=THT]
  R1 = Resistor [tolerance=±5% resistance=3.3k package=THT]
  DMX_IN = XLR3_NCFAH2 [package=xlr3_nc3fah2]
  U2 = MAX485 [package=dil08]
  DMX_OUT = XLR3_NCFAH2 [package=xlr3_nc3fah2]
  reset = SWITCH-MOMENTARY-2 [package=tactile-pth]
  SS = SPST Switch [package=ayz0202]

nets:
  N1: U1.RO, Atmega162.PD0
  GND: U1.RE, U1.DE, U1.GND, Atmega162.GND, Raspberry_Pi_1.GND, R1.Pin_0, reset.2, SS.O
  N2: U1.A, DMX_IN.3
  N3: U1.B, DMX_IN.2
  VCC: U1.VCC, Raspberry_Pi_1.5V, U2.RE, U2.DE, U2.VCC
  N4: Atmega162.PB2, Raspberry_Pi_1.GIPO14
  N5: Atmega162.PB3, R2.Pin_1
  N6: Atmega162.PB4, SS.P
  N7: Atmega162.PB5, Raspberry_Pi_1.GIPO23
  N8: Atmega162.PB6, Raspberry_Pi_1.GIPO18
  N9: Atmega162.PB7, Raspberry_Pi_1.GIPO24
  N10: Atmega162.RESET, Raspberry_Pi_1.GIPO12, reset.1
  N11: Atmega162.PD1, U2.DI
  3V3: Atmega162.VCC, Raspberry_Pi_1.3v3, Raspberry_Pi_1.3V3
  N12: Raspberry_Pi_1.GIPO15, R2.Pin_0, R1.Pin_1
  N13: DMX_IN.1, DMX_IN.G, U2.GND, DMX_OUT.1, DMX_OUT.G
  N14: U2.A, DMX_OUT.3
  N15: U2.B, DMX_OUT.2

custom parts:
  ATmega162: AVR 8-bit microcontroller.

// code stored in the sketch: Scetch for board.ino

